# Fritzing sketch esquema agente captacion (saved by Fritzing 0.9.3b)
breadboards: 1

parts:
  hc-sr1 = hc-sr04
  WeMos_D1_Mini1 = WeMos D1 Mini
  Componente1 = RFID-RC522-v3 [part_number=RFID-RC522]
  LED1 = LED - 5mm [color="Green (555nm)" package="5 mm [THT]"]
  LED2 = smd LED [color="Red (633nm)" package="0603 [SMD]"]

nets:
  VCC: hc-sr1.VCC, WeMos_D1_Mini1.5V
  N1: hc-sr1.Trig, WeMos_D1_Mini1.D1
  N2: hc-sr1.Echo, WeMos_D1_Mini1.D2
  GND: hc-sr1.GND, WeMos_D1_Mini1.G, Componente1.GND, LED1.cathode, LED2.cathode
  3V3: WeMos_D1_Mini1.3V3, Componente1.3.3V
  N3: WeMos_D1_Mini1.D3, Componente1.RST
  N4: WeMos_D1_Mini1.D5, Componente1.SCK
  N5: WeMos_D1_Mini1.D6, Componente1.MISO
  N6: WeMos_D1_Mini1.D7, Componente1.MOSI
  N7: WeMos_D1_Mini1.D8, Componente1.SDA
  N8: WeMos_D1_Mini1.RX, LED1.anode
  N9: WeMos_D1_Mini1.TX, LED2.anode

custom parts:
  RFID-RC522-v3: A simple China made RFID-RC522 Reader (6x4 cm); do check the pin labels, as this is a MFRC522 based clone.
